// Logisim project Fix CDM.circ as structural Verilog: 12 circuits, main circuit main
module main (
);

  wire Ball_color_out, Ball_weight_out, clock_1_out, game_end_screen_and_settings_1__0,
       game_end_screen_and_settings_1__1, game_end_screen_and_settings_1__2,
       game_end_screen_and_settings_1_heavy, game_end_screen_and_settings_1_light,
       kinematic_controller_1_out_15, kinematic_controller_1_out_16, Level_out, Reset_out, Start_out,
       video_section_1_out_23, video_section_2_out_23, video_section_3_out_23;
  wire [3:0] db, dp, game_end_screen_and_settings_1_settings, sb, sp;
  wire [4:0] joystick_1_y, kinematic_controller_1_ballx, kinematic_controller_1_chipid,
       video_section_1_id_output, video_section_1_x_output, video_section_2_id_output,
       video_section_2_x_output, video_section_3_id_output, video_section_3_x_output;
  wire [31:0] game_end_screen_and_settings_1_out_5, game_end_screen_and_settings_1_out_6,
       game_end_screen_and_settings_1_out_7, game_end_screen_and_settings_1_out_8,
       game_end_screen_and_settings_1_out_9, game_end_screen_and_settings_1_out_10,
       game_end_screen_and_settings_1_out_11, game_end_screen_and_settings_1_out_12,
       game_end_screen_and_settings_1_out_13, game_end_screen_and_settings_1_out_14,
       game_end_screen_and_settings_1_out_15, game_end_screen_and_settings_1_out_16,
       game_end_screen_and_settings_1_out_17, game_end_screen_and_settings_1_out_18,
       game_end_screen_and_settings_1_out_19, game_end_screen_and_settings_1_out_20,
       game_end_screen_and_settings_1_out_21, game_end_screen_and_settings_1_out_22,
       game_end_screen_and_settings_1_out_23, game_end_screen_and_settings_1_out_24,
       game_end_screen_and_settings_1_out_25, game_end_screen_and_settings_1_out_26,
       game_end_screen_and_settings_1_out_27, game_end_screen_and_settings_1_out_28,
       game_end_screen_and_settings_1_out_29, game_end_screen_and_settings_1_out_30,
       game_end_screen_and_settings_1_out_31, game_end_screen_and_settings_1_out_32,
       game_end_screen_and_settings_1_out_33, game_end_screen_and_settings_1_out_34,
       game_end_screen_and_settings_1_out_35, game_end_screen_and_settings_1_out_36,
       kinematic_controller_1_bally, kinematic_controller_1_left_bat, kinematic_controller_1_right_bat,
       video_section_1_left_bat_2, video_section_1_out_15, video_section_1_out_16, video_section_1_out_17,
       video_section_1_out_18, video_section_1_out_19, video_section_1_out_20, video_section_1_out_21,
       video_section_1_out_22, video_section_1_right_bat_2, video_section_1_y_output,
       video_section_2_left_bat_2, video_section_2_out_15, video_section_2_out_16, video_section_2_out_17,
       video_section_2_out_18, video_section_2_out_19, video_section_2_out_20, video_section_2_out_21,
       video_section_2_out_22, video_section_2_right_bat_2, video_section_2_y_output,
       video_section_3_left_bat_2, video_section_3_out_15, video_section_3_out_16, video_section_3_out_17,
       video_section_3_out_18, video_section_3_out_19, video_section_3_out_20, video_section_3_out_21,
       video_section_3_out_22, video_section_3_right_bat_2, video_section_3_y_output, video_section_4_out_15,
       video_section_4_out_16, video_section_4_out_17, video_section_4_out_18, video_section_4_out_19,
       video_section_4_out_20, video_section_4_out_21, video_section_4_out_22;

  Hex_Digit_Display hex_digit_display_1 (.value(dp));  // open: dp
  Button Start (.out(Start_out));
  Joystick #(.bits(5)) joystick_1 (.y(joystick_1_y));  // open: x
  Clock clock_1 (.out(clock_1_out));
  Hex_Digit_Display hex_digit_display_2 (.value(sp));  // open: dp
  Button Reset (.out(Reset_out));
  DotMatrix #(.matrixcols(32), .matrixrows(32)) dotmatrix_1 (
    .col0(video_section_1_out_15), .col1(video_section_1_out_16), .col2(video_section_1_out_17),
    .col3(video_section_1_out_18), .col4(video_section_1_out_19), .col5(video_section_1_out_20),
    .col6(video_section_1_out_21), .col7(video_section_1_out_22), .col8(video_section_2_out_15),
    .col9(video_section_2_out_16), .col10(video_section_2_out_17), .col11(video_section_2_out_18),
    .col12(video_section_2_out_19), .col13(video_section_2_out_20), .col14(video_section_2_out_21),
    .col15(video_section_2_out_22), .col16(video_section_3_out_15), .col17(video_section_3_out_16),
    .col18(video_section_3_out_17), .col19(video_section_3_out_18), .col20(video_section_3_out_19),
    .col21(video_section_3_out_20), .col22(video_section_3_out_21), .col23(video_section_3_out_22),
    .col24(video_section_4_out_15), .col25(video_section_4_out_16), .col26(video_section_4_out_17),
    .col27(video_section_4_out_18), .col28(video_section_4_out_19), .col29(video_section_4_out_20),
    .col30(video_section_4_out_21), .col31(video_section_4_out_22));
  kinematic_controller kinematic_controller_1 (
    .joistic(joystick_1_y), .start(Start_out), .reset(Reset_out), .chipID(kinematic_controller_1_chipid),
    .ballY(kinematic_controller_1_bally), .ballX(kinematic_controller_1_ballx),
    .left_bat(kinematic_controller_1_left_bat), .right_bat(kinematic_controller_1_right_bat),
    .out_15(kinematic_controller_1_out_15), .out_16(kinematic_controller_1_out_16),
    .settings(game_end_screen_and_settings_1_settings), .clk(clock_1_out), .Single_digits_p(sp),
    .Single_digits_b(sb), .Decimal_digit_b(db), .Decimal_digit_p(dp));
  game_end_screen_and_settings game_end_screen_and_settings_1 (
    .out_5(game_end_screen_and_settings_1_out_5), .out_6(game_end_screen_and_settings_1_out_6),
    .out_7(game_end_screen_and_settings_1_out_7), .out_8(game_end_screen_and_settings_1_out_8),
    .out_9(game_end_screen_and_settings_1_out_9), .out_10(game_end_screen_and_settings_1_out_10),
    .out_11(game_end_screen_and_settings_1_out_11), .out_12(game_end_screen_and_settings_1_out_12),
    .out_13(game_end_screen_and_settings_1_out_13), .out_14(game_end_screen_and_settings_1_out_14),
    .out_15(game_end_screen_and_settings_1_out_15), .out_16(game_end_screen_and_settings_1_out_16),
    .out_17(game_end_screen_and_settings_1_out_17), .out_18(game_end_screen_and_settings_1_out_18),
    .out_19(game_end_screen_and_settings_1_out_19), .out_20(game_end_screen_and_settings_1_out_20),
    .out_21(game_end_screen_and_settings_1_out_21), .out_22(game_end_screen_and_settings_1_out_22),
    .out_23(game_end_screen_and_settings_1_out_23), .out_24(game_end_screen_and_settings_1_out_24),
    .out_25(game_end_screen_and_settings_1_out_25), .out_26(game_end_screen_and_settings_1_out_26),
    .out_27(game_end_screen_and_settings_1_out_27), .out_28(game_end_screen_and_settings_1_out_28),
    .out_29(game_end_screen_and_settings_1_out_29), .out_30(game_end_screen_and_settings_1_out_30),
    .out_31(game_end_screen_and_settings_1_out_31), .out_32(game_end_screen_and_settings_1_out_32),
    .out_33(game_end_screen_and_settings_1_out_33), .out_34(game_end_screen_and_settings_1_out_34),
    .out_35(game_end_screen_and_settings_1_out_35), .out_36(game_end_screen_and_settings_1_out_36),
    .in_1(kinematic_controller_1_out_16), .Color(Ball_color_out), .Weight(Ball_weight_out),
    .\Сomplexity (Level_out), ._0(game_end_screen_and_settings_1__0), ._1(game_end_screen_and_settings_1__1),
    ._2(game_end_screen_and_settings_1__2), .Light(game_end_screen_and_settings_1_light),
    .Heavy(game_end_screen_and_settings_1_heavy), .Settings(game_end_screen_and_settings_1_settings));
  Button Ball_weight (.out(Ball_weight_out));
  video_section video_section_1 (
    .ID_output(video_section_1_id_output), .X_output(video_section_1_x_output),
    .Y_output(video_section_1_y_output), .Left_bat_2(video_section_1_left_bat_2),
    .Right_bat_2(video_section_1_right_bat_2), .ID_input(kinematic_controller_1_chipid),
    .X_ball(kinematic_controller_1_ballx), .Y_ball(kinematic_controller_1_bally),
    .Left_bat(kinematic_controller_1_left_bat), .Right_bat(kinematic_controller_1_right_bat),
    .in_7(game_end_screen_and_settings_1_out_5), .in_8(game_end_screen_and_settings_1_out_6),
    .in_9(game_end_screen_and_settings_1_out_7), .in_10(game_end_screen_and_settings_1_out_8),
    .in_11(game_end_screen_and_settings_1_out_9), .in_12(game_end_screen_and_settings_1_out_10),
    .in_13(game_end_screen_and_settings_1_out_11), .in_14(game_end_screen_and_settings_1_out_12),
    .out_15(video_section_1_out_15), .out_16(video_section_1_out_16), .out_17(video_section_1_out_17),
    .out_18(video_section_1_out_18), .out_19(video_section_1_out_19), .out_20(video_section_1_out_20),
    .out_21(video_section_1_out_21), .out_22(video_section_1_out_22), .in_1(kinematic_controller_1_out_15),
    .out_23(video_section_1_out_23));
  LED led_1 (.in(game_end_screen_and_settings_1_light));
  video_section video_section_2 (
    .ID_output(video_section_2_id_output), .X_output(video_section_2_x_output),
    .Y_output(video_section_2_y_output), .Left_bat_2(video_section_2_left_bat_2),
    .Right_bat_2(video_section_2_right_bat_2), .ID_input(video_section_1_id_output),
    .X_ball(video_section_1_x_output), .Y_ball(video_section_1_y_output),
    .Left_bat(video_section_1_left_bat_2), .Right_bat(video_section_1_right_bat_2),
    .in_7(game_end_screen_and_settings_1_out_13), .in_8(game_end_screen_and_settings_1_out_14),
    .in_9(game_end_screen_and_settings_1_out_15), .in_10(game_end_screen_and_settings_1_out_16),
    .in_11(game_end_screen_and_settings_1_out_17), .in_12(game_end_screen_and_settings_1_out_18),
    .in_13(game_end_screen_and_settings_1_out_19), .in_14(game_end_screen_and_settings_1_out_20),
    .out_15(video_section_2_out_15), .out_16(video_section_2_out_16), .out_17(video_section_2_out_17),
    .out_18(video_section_2_out_18), .out_19(video_section_2_out_19), .out_20(video_section_2_out_20),
    .out_21(video_section_2_out_21), .out_22(video_section_2_out_22), .in_1(video_section_1_out_23),
    .out_23(video_section_2_out_23));
  Button Level (.out(Level_out));
  LED led_2 (.in(game_end_screen_and_settings_1_heavy));
  video_section video_section_3 (
    .ID_output(video_section_3_id_output), .X_output(video_section_3_x_output),
    .Y_output(video_section_3_y_output), .Left_bat_2(video_section_3_left_bat_2),
    .Right_bat_2(video_section_3_right_bat_2), .ID_input(video_section_2_id_output),
    .X_ball(video_section_2_x_output), .Y_ball(video_section_2_y_output),
    .Left_bat(video_section_2_left_bat_2), .Right_bat(video_section_2_right_bat_2),
    .in_7(game_end_screen_and_settings_1_out_21), .in_8(game_end_screen_and_settings_1_out_22),
    .in_9(game_end_screen_and_settings_1_out_23), .in_10(game_end_screen_and_settings_1_out_24),
    .in_11(game_end_screen_and_settings_1_out_25), .in_12(game_end_screen_and_settings_1_out_26),
    .in_13(game_end_screen_and_settings_1_out_27), .in_14(game_end_screen_and_settings_1_out_28),
    .out_15(video_section_3_out_15), .out_16(video_section_3_out_16), .out_17(video_section_3_out_17),
    .out_18(video_section_3_out_18), .out_19(video_section_3_out_19), .out_20(video_section_3_out_20),
    .out_21(video_section_3_out_21), .out_22(video_section_3_out_22), .in_1(video_section_2_out_23),
    .out_23(video_section_3_out_23));
  LED led_3 (.in(game_end_screen_and_settings_1__2));
  LED led_4 (.in(game_end_screen_and_settings_1__0));
  LED led_5 (.in(game_end_screen_and_settings_1__1));
  Hex_Digit_Display hex_digit_display_3 (.value(db));  // open: dp
  video_section video_section_4 (
    .ID_input(video_section_3_id_output), .X_ball(video_section_3_x_output),
    .Y_ball(video_section_3_y_output), .Left_bat(video_section_3_left_bat_2),
    .Right_bat(video_section_3_right_bat_2), .in_7(game_end_screen_and_settings_1_out_29),
    .in_8(game_end_screen_and_settings_1_out_30), .in_9(game_end_screen_and_settings_1_out_31),
    .in_10(game_end_screen_and_settings_1_out_32), .in_11(game_end_screen_and_settings_1_out_33),
    .in_12(game_end_screen_and_settings_1_out_34), .in_13(game_end_screen_and_settings_1_out_35),
    .in_14(game_end_screen_and_settings_1_out_36), .out_15(video_section_4_out_15),
    .out_16(video_section_4_out_16), .out_17(video_section_4_out_17), .out_18(video_section_4_out_18),
    .out_19(video_section_4_out_19), .out_20(video_section_4_out_20), .out_21(video_section_4_out_21),
    .out_22(video_section_4_out_22), .in_1(video_section_3_out_23));  // open: ID_output, X_output, Y_output, Left_bat_2, Right_bat_2, out_23
  Button Ball_color (.out(Ball_color_out));
  Hex_Digit_Display hex_digit_display_4 (.value(sb));  // open: dp

  // Notes on the sheet:
  //   Light
  //   Heavy
endmodule

module kinematic_controller (
  input  [4:0] joistic,
  input  clk,
  input  start,
  input  reset,
  input  [3:0] settings,
  output [4:0] chipID,
  output [31:0] ballY,
  output [4:0] ballX,
  output [31:0] left_bat,
  output [31:0] right_bat,
  output [3:0] Single_digits_b,
  output [3:0] Single_digits_p,
  output [3:0] Decimal_digit_b,
  output [3:0] Decimal_digit_p,
  output out_15,
  output out_16
);

  wire and_2_out, and_3_out, and_4_out, and_5_out, clock, comparator_3_gt, comparator_4_gt,
       controlled_buffer_1_out, controlled_buffer_2_out, controlled_buffer_3_out, controlled_buffer_4_out,
       controlled_buffer_5_out, d_ff_1_q, freeze, game_over, Left_bat_reflection, Left_goal, lose, not_2_out,
       not_3_out, not_4_out, not_5_out, not_6_out, not_7_out, or_1_out, Right_bat_reflection, Right_goal,
       run, start_pos, transistor_1_out, xor_1_out;
  wire [2:0] demultiplexer_1_out0, demultiplexer_1_out1, not_1_out, Speed_Left_bat;
  wire [3:0] counter_3_q, Speed_right_bat;
  wire [4:0] multiplexer_4_out, n8_to_5_1_out_2, n8_to_5_2_out_2, n8_to_5_4_out_2, new_speed, speed;
  wire [7:0] ball_X_pos, ball_Y_pos, Calced_ball_Y, current_right_bat, inc_score_1_output,
       inc_score_2_output, multiplexer_2_out, multiplexer_3_out, multiplexer_5_out, multiplexer_6_out,
       new_ball_X_pos, new_ball_Y_pos, new_left_bat, newt_right_bat, \сurrent_left_bat ;

  Demultiplexer #(.width(3), .enable("false")) demultiplexer_1 (
    .out0(demultiplexer_1_out0), .out1(demultiplexer_1_out1), .in(joistic[3:1]), .sel(joistic[4]));
  Demultiplexer #(.select(5), .disabled(0), .enable("false")) demultiplexer_2 (
    .out0(ballY[0]), .out1(ballY[1]), .out2(ballY[2]), .out3(ballY[3]), .out4(ballY[4]), .out5(ballY[5]),
    .out6(ballY[6]), .out7(ballY[7]), .out8(ballY[8]), .out9(ballY[9]), .out10(ballY[10]), .out11(ballY[11]),
    .out12(ballY[12]), .out13(ballY[13]), .out14(ballY[14]), .out15(ballY[15]), .out16(ballY[16]),
    .out17(ballY[17]), .out18(ballY[18]), .out19(ballY[19]), .out20(ballY[20]), .out21(ballY[21]),
    .out22(ballY[22]), .out23(ballY[23]), .out24(ballY[24]), .out25(ballY[25]), .out26(ballY[26]),
    .out27(ballY[27]), .out28(ballY[28]), .out29(ballY[29]), .out30(ballY[30]), .out31(ballY[31]),
    .in(transistor_1_out), .sel(n8_to_5_1_out_2));
  Transistor transistor_1 (.in(1'b1), .out(transistor_1_out), .gate(settings[3]));
  assign not_1_out = ~demultiplexer_1_out0;  // NOT_Gate not_1, 3 bits wide
  Multiplexer #(.width(3), .enable("false")) multiplexer_1 (
    .in0(not_1_out), .in1(demultiplexer_1_out1), .out(Speed_Left_bat), .sel(joistic[4]));
  Counter #(.width(3), .max('h4)) counter_1 (.carry(clock), .clk(clk));  // open: load, D, count, Q, clr
  not not_2 (not_2_out, run);
  Counter #(.width(1), .max('h1)) counter_2 (
    .count(not_2_out), .carry(run), .clk(start), .clr(reset));  // open: load, D, Q
  _8_to_5 u_8_to_5_1 (.in_1(ball_Y_pos), .out_2(n8_to_5_1_out_2));
  _8_to_5 u_8_to_5_2 (.in_1(\сurrent_left_bat ), .out_2(n8_to_5_2_out_2));
  _8_to_5 u_8_to_5_3 (.in_1(ball_X_pos), .out_2(ballX));
  _8_to_5 u_8_to_5_4 (.in_1(current_right_bat), .out_2(n8_to_5_4_out_2));
  Shifter #(.width(32)) shifter_1 (.in(32'hf), .\dist (n8_to_5_2_out_2), .out(left_bat));
  Shifter #(.width(32)) shifter_2 (.in(32'hf), .\dist (n8_to_5_4_out_2), .out(right_bat));
  and and_1 (out_15, freeze, game_over);
  Comparator #(.mode("unsigned")) comparator_1 (.a(8'hf7), .b(ball_X_pos), .lt(Right_goal));  // open: gt, eq
  Comparator #(.mode("unsigned")) comparator_2 (.a(8'h8), .b(ball_X_pos), .gt(Left_goal));  // open: eq, lt
  Multiplexer #(.width(8), .enable("false")) multiplexer_2 (
    .in0(8'h80), .in1(new_ball_X_pos), .out(multiplexer_2_out), .sel(and_2_out));
  and and_2 (and_2_out, ~start_pos, run);  // AND_Gate
  Multiplexer #(.width(8), .enable("false")) multiplexer_3 (
    .in0(8'h80), .in1(new_ball_Y_pos), .out(multiplexer_3_out), .sel(and_3_out));
  and and_3 (and_3_out, ~start_pos, run);  // AND_Gate
  Multiplexer #(.width(5), .enable("false")) multiplexer_4 (
    .in0(5'b11000), .in1(new_speed), .out(multiplexer_4_out), .sel(and_4_out));
  and and_4 (and_4_out, ~start_pos, run);  // AND_Gate
  Multiplexer #(.width(8), .enable("false")) multiplexer_5 (
    .in0(8'h78), .in1(new_left_bat), .out(multiplexer_5_out), .sel(run));
  Multiplexer #(.width(8), .enable("false")) multiplexer_6 (
    .in0(8'h78), .in1(newt_right_bat), .out(multiplexer_6_out), .sel(run));
  Register register_1 (.D(multiplexer_2_out), .en(freeze), .Q(ball_X_pos), .clk(controlled_buffer_1_out));  // open: clr
  assign controlled_buffer_1_out = not_3_out ? clock : 1'bz;  // Controlled_Buffer controlled_buffer_1
  not not_3 (not_3_out, game_over);
  Register register_2 (.D(multiplexer_3_out), .en(freeze), .Q(ball_Y_pos), .clk(controlled_buffer_2_out));  // open: clr
  assign controlled_buffer_2_out = not_4_out ? clock : 1'bz;  // Controlled_Buffer controlled_buffer_2
  not not_4 (not_4_out, game_over);
  Register #(.width(5)) register_3 (
    .D(multiplexer_4_out), .en(freeze), .Q(speed), .clk(controlled_buffer_3_out));  // open: clr
  assign controlled_buffer_3_out = not_5_out ? clock : 1'bz;  // Controlled_Buffer controlled_buffer_3
  not not_5 (not_5_out, game_over);
  Register register_4 (
    .D(multiplexer_5_out), .en(freeze), .Q(\сurrent_left_bat ), .clk(controlled_buffer_4_out));  // open: clr
  assign controlled_buffer_4_out = not_6_out ? clock : 1'bz;  // Controlled_Buffer controlled_buffer_4
  not not_6 (not_6_out, game_over);
  Register register_5 (
    .D(multiplexer_6_out), .en(freeze), .Q(current_right_bat), .clk(controlled_buffer_5_out));  // open: clr
  assign controlled_buffer_5_out = not_7_out ? clock : 1'bz;  // Controlled_Buffer controlled_buffer_5
  not not_7 (not_7_out, game_over);
  inc_score inc_score_1 (.\input ({Decimal_digit_b, Single_digits_b}), .\output (inc_score_1_output));
  Register register_6 (
    .D(inc_score_1_output), .Q({Decimal_digit_b, Single_digits_b}), .clk(Left_goal), .clr(reset));  // open: en
  game_over game_over_1 (
    .player({Decimal_digit_p, Single_digits_p}), .cdm8({Decimal_digit_b, Single_digits_b}), .win(out_16),
    .game_over(game_over), .lose(lose));
  Counter #(.width(4), .max('hf), .ongoal("stay"), .trigger("falling")) counter_3 (
    .Q(counter_3_q), .clk(clock), .clr(and_5_out));  // open: load, D, count, carry
  D_Flip_Flop d_ff_1 (.clk(clock), .D(or_1_out), .Q(d_ff_1_q));  // open: Qn, preset, en, reset
  or or_1 (or_1_out, Right_goal, Left_goal);
  inc_score inc_score_2 (.\input ({Decimal_digit_p, Single_digits_p}), .\output (inc_score_2_output));
  Register register_7 (
    .D(inc_score_2_output), .Q({Decimal_digit_p, Single_digits_p}), .clk(Right_goal), .clr(reset));  // open: en
  calculating_circuit calculating_circuit_1 (
    .X_ball(ball_X_pos), .New_X_ball(new_ball_X_pos), .Y_ball(ball_Y_pos), .New_Y_ball(new_ball_Y_pos),
    .V(speed), .New_V(new_speed), .Left_bat(\сurrent_left_bat ), .New_Left_bat(new_left_bat),
    .Speed_Left_bat({joistic[4], Speed_Left_bat}), .Right_bat(current_right_bat),
    .New_Right_bat(newt_right_bat), .Speed_Right_bat(Speed_right_bat),
    .Right_bat_reflection(Right_bat_reflection), .Left_bat_reflection(Left_bat_reflection), .in_3(settings[0]));
  CDM8_bat_move cdm8_bat_move_1 (
    .Current_bat_pos(current_right_bat), .New_bat_pos(Calced_ball_Y), .Level(settings[2:1]),
    .Right_bat_speed(Speed_right_bat), .X_speed_direction(speed[4]), .Current_X_pos(ball_X_pos),
    .left_bat_reflection(Left_bat_reflection));
  Comparator #(.width(4), .mode("unsigned")) comparator_3 (
    .a(4'b1000), .b(counter_3_q), .gt(comparator_3_gt));  // open: eq, lt
  Comparator #(.width(4), .mode("unsigned")) comparator_4 (
    .a(4'b1111), .b(counter_3_q), .gt(comparator_4_gt));  // open: eq, lt
  and and_5 (and_5_out, ~start_pos, xor_1_out);  // AND_Gate
  xor xor_1 (xor_1_out, d_ff_1_q, or_1_out);
  not not_8 (freeze, comparator_3_gt);
  and and_6 (start_pos, ~comparator_3_gt, comparator_4_gt);  // AND_Gate
  CDM8 cdm8_1 (.BallX(ball_X_pos), .BallY(ball_Y_pos), .speed(speed), .calc_bat_pos(Calced_ball_Y), .in_1(clk));

  assign chipID = {5{1'b0}};

  // Other names for the same wires on the sheet: clock1 = clk; cs[7:0] = {Decimal_digit_p, Single_digits_p};
  //   ps[7:0] = {Decimal_digit_b, Single_digits_b}; weight = settings[0]; level[1:0] = settings[2:1];
  //   ball_color = settings[3]; Speed_Left_bat[3] = joistic[4]; win = out_16

  // Notes on the sheet:
  //   Input
  //   Output
  //   Generating
  //   Score
  //   Calculating
  //   Processor
endmodule

module CDM8_bat_move (
  input  [7:0] New_bat_pos,
  input  [7:0] Current_bat_pos,
  input  left_bat_reflection,
  input  X_speed_direction,
  input  [1:0] Level,
  input  [7:0] Current_X_pos,
  output [3:0] Right_bat_speed
);

  wire adder_3_cout, and_1_out, and_2_out, comparator_1_eq, comparator_1_gt, comparator_1_lt,
       comparator_2_gt, comparator_3_gt, or_1_out, subtractor_1_bout;
  wire [1:0] random_speed;
  wire [3:0] bit_extender_2_out, multiplexer_5_out, multiplexer_6_out, random_1_out;
  wire [4:0] n8_to_5_1_out_2, n8_to_5_2_out_2;
  wire [7:0] adder_1_out, adder_2_out, adder_3_out, bit_extender_1_out, demultiplexer_1_out0,
       demultiplexer_1_out1, demultiplexer_2_out0, demultiplexer_2_out1, multiplexer_1_out,
       multiplexer_2_out, multiplexer_3_out, multiplexer_4_out, subtractor_1_out;

  Random #(.width(4), .seed(4532)) random_1 (.clk(left_bat_reflection), .out(random_1_out));  // open: next, clr
  Random #(.width(2), .seed(3245)) random_2 (.clk(left_bat_reflection), .out(random_speed));  // open: next, clr
  Demultiplexer #(.select(2), .width(8), .enable("false")) demultiplexer_1 (
    .out0(demultiplexer_1_out0), .out1(demultiplexer_1_out1), .in(bit_extender_1_out), .sel(Level));  // open: out2, out3
  assign bit_extender_1_out = {{5{1'b0}}, random_1_out[2:0]};  // Bit_Extender bit_extender_1
  Adder adder_1 (.a(demultiplexer_1_out0), .b(8'h6), .out(adder_1_out));  // open: cin, cout
  Adder adder_2 (.a(demultiplexer_1_out1), .b(8'h3), .out(adder_2_out));  // open: cin, cout
  Multiplexer #(.select(2), .width(8), .enable("false")) multiplexer_1 (
    .in0(adder_1_out), .in1(adder_2_out), .in2({8{1'b0}}), .out(multiplexer_1_out), .sel(Level));  // open: in3
  Demultiplexer #(.width(8), .enable("false")) demultiplexer_2 (
    .out0(demultiplexer_2_out0), .out1(demultiplexer_2_out1), .in(multiplexer_1_out), .sel(random_1_out[3]));
  Adder adder_3 (.a(New_bat_pos), .b(demultiplexer_2_out0), .out(adder_3_out), .cout(adder_3_cout));  // open: cin
  Multiplexer #(.width(8), .enable("false")) multiplexer_2 (
    .in0(adder_3_out), .in1({8{1'b1}}), .out(multiplexer_2_out), .sel(adder_3_cout));
  Subtractor subtractor_1 (
    .a(New_bat_pos), .b(demultiplexer_2_out1), .out(subtractor_1_out), .bout(subtractor_1_bout));  // open: bin
  Multiplexer #(.width(8), .enable("false")) multiplexer_3 (
    .in0(subtractor_1_out), .in1({8{1'b0}}), .out(multiplexer_3_out), .sel(subtractor_1_bout));
  Multiplexer #(.width(8), .enable("false")) multiplexer_4 (
    .in0(multiplexer_2_out), .in1(multiplexer_3_out), .out(multiplexer_4_out), .sel(random_1_out[3]));
  _8_to_5 u_8_to_5_1 (.in_1(multiplexer_4_out), .out_2(n8_to_5_1_out_2));
  _8_to_5 u_8_to_5_2 (.in_1(Current_bat_pos), .out_2(n8_to_5_2_out_2));
  Comparator #(.width(5), .mode("unsigned")) comparator_1 (
    .a(n8_to_5_1_out_2), .b(n8_to_5_2_out_2), .gt(comparator_1_gt), .eq(comparator_1_eq), .lt(comparator_1_lt));
  Multiplexer #(.width(4), .enable("false")) multiplexer_5 (
    .in0(4'b0000), .in1(4'b0111), .out(multiplexer_5_out), .sel(comparator_1_gt));
  Comparator #(.mode("unsigned")) comparator_2 (.a(Current_X_pos), .b(8'hf3), .gt(comparator_2_gt));  // open: eq, lt
  Comparator #(.mode("unsigned")) comparator_3 (.a(Current_X_pos), .b(8'hc8), .gt(comparator_3_gt));  // open: eq, lt
  Multiplexer #(.width(4), .enable("false")) multiplexer_6 (
    .in0(multiplexer_5_out), .in1(4'b1111), .out(multiplexer_6_out), .sel(comparator_1_lt));
  and and_1 (and_1_out, comparator_1_eq, ~X_speed_direction, comparator_2_gt);  // AND_Gate
  and and_2 (and_2_out, X_speed_direction, comparator_3_gt);
  Multiplexer #(.width(4), .enable("false")) multiplexer_7 (
    .in0(multiplexer_6_out), .in1(bit_extender_2_out), .out(Right_bat_speed), .sel(or_1_out));
  assign bit_extender_2_out = {{2{1'b1}}, random_speed};  // Bit_Extender bit_extender_2
  or or_1 (or_1_out, and_1_out, and_2_out);
endmodule

module calculating_circuit (
  input  [7:0] X_ball,
  input  [7:0] Y_ball,
  input  in_3,
  input  [4:0] V,
  input  [7:0] Left_bat,
  input  [3:0] Speed_Left_bat,
  input  [7:0] Right_bat,
  input  [3:0] Speed_Right_bat,
  output Right_bat_reflection,
  output [7:0] New_X_ball,
  output Left_bat_reflection,
  output [7:0] New_Y_ball,
  output [4:0] New_V,
  output [7:0] New_Left_bat,
  output [7:0] New_Right_bat
);

  wire adder_2_cout, and_5_out, Change_X_direction, Change_Y_direction, comparator_1_gt, comparator_2_lt,
       comparator_3_gt, comparator_4_gt, comparator_5_eq, comparator_6_eq, Left_bat_Y_collision,
       Left_changed, New_Y_direction, Right_bat_Y_collision, Right_changed, subtractor_2_bout,
       subtractor_3_bout, subtractor_4_bout, subtractor_7_bout;
  wire [1:0] and_3_out, xor_3_out;
  wire [2:0] bit_extender_7_out, bit_extender_8_out, demultiplexer_9_out2;
  wire [3:0] demultiplexer_9_out0, demultiplexer_9_out1, demultiplexer_9_out3, multiplexer_1_out;
  wire [3:3] demultiplexer_9_out2_2, xor_4_out;
  wire [4:0] n8_to_5_2_out_2, n8_to_5_3_out_2, New_Y_ball5;
  wire [7:0] adder_1_out, adder_2_out, adder_3_out, adder_4_out, adder_5_out, adder_6_out, adder_7_out,
       bit_extender_1_out, bit_extender_2_out, bit_extender_3_out, bit_extender_4_out, bit_extender_5_out,
       bit_extender_6_out, demultiplexer_1_out0, demultiplexer_1_out1, demultiplexer_2_out0,
       demultiplexer_2_out1, demultiplexer_3_out0, demultiplexer_3_out1, demultiplexer_4_out0,
       demultiplexer_4_out1, demultiplexer_5_out0, demultiplexer_5_out1, demultiplexer_6_out0,
       demultiplexer_6_out1, demultiplexer_7_out0, demultiplexer_7_out1, demultiplexer_8_out0,
       demultiplexer_8_out1, devision_with_rounding_1_out_3, devision_with_rounding_2_out_3,
       multiplexer_2_out, multiplexer_3_out, multiplexer_4_out, multiplexer_5_out, multiplexer_6_out,
       multiplexer_7_out, multiplexer_11_out, multiplexer_13_out, multiplexer_14_out, multiplexer_15_out,
       multiplexer_16_out, multiplier_1_out, multiplier_2_out, multiplier_3_out, negator_1_out,
       negator_2_out, not_1_out, not_2_out, not_3_out, subtractor_1_out, subtractor_2_out, subtractor_3_out,
       subtractor_4_out, subtractor_5_out, subtractor_6_out, subtractor_7_out;
  wire [31:0] shifter_1_out, shifter_2_out;

  Demultiplexer #(.width(8), .disabled(0), .enable("false")) demultiplexer_1 (
    .out0(demultiplexer_1_out0), .out1(demultiplexer_1_out1), .in(X_ball), .sel(V[4]));
  Demultiplexer #(.width(8), .disabled(0), .enable("false")) demultiplexer_2 (
    .out0(demultiplexer_2_out0), .out1(demultiplexer_2_out1), .in(Y_ball), .sel(V[3]));
  Demultiplexer #(.width(8), .disabled(0), .enable("false")) demultiplexer_3 (
    .out0(demultiplexer_3_out0), .out1(demultiplexer_3_out1), .in(Left_bat), .sel(Speed_Left_bat[3]));
  assign bit_extender_1_out = {{5{1'b0}}, Speed_Left_bat[2:0]};  // Bit_Extender bit_extender_1
  Demultiplexer #(.width(8), .disabled(0), .enable("false")) demultiplexer_4 (
    .out0(demultiplexer_4_out0), .out1(demultiplexer_4_out1), .in(Right_bat), .sel(Speed_Right_bat[3]));
  assign bit_extender_2_out = {{5{1'b0}}, Speed_Right_bat[2:0]};  // Bit_Extender bit_extender_2
  assign bit_extender_3_out = {{5{1'b0}}, V[2:0]};  // Bit_Extender bit_extender_3
  Adder adder_1 (.a(demultiplexer_1_out0), .b(8'h4), .out(adder_1_out));  // open: cin, cout
  Subtractor subtractor_1 (.a(demultiplexer_1_out1), .b(8'h4), .out(subtractor_1_out));  // open: bin, bout
  Adder adder_2 (
    .a(demultiplexer_2_out0), .b(bit_extender_3_out), .out(adder_2_out), .cout(adder_2_cout));  // open: cin
  Demultiplexer #(.width(8), .disabled(0), .enable("false")) demultiplexer_5 (
    .out0(demultiplexer_5_out0), .out1(demultiplexer_5_out1), .in(adder_2_out), .sel(adder_2_cout));
  Subtractor subtractor_2 (
    .a(demultiplexer_2_out1), .b(bit_extender_3_out), .out(subtractor_2_out), .bout(subtractor_2_bout));  // open: bin
  Demultiplexer #(.width(8), .disabled(0), .enable("false")) demultiplexer_6 (
    .out0(demultiplexer_6_out0), .out1(demultiplexer_6_out1), .in(subtractor_2_out), .sel(subtractor_2_bout));
  Adder adder_3 (.a(demultiplexer_3_out0), .b(bit_extender_1_out), .out(adder_3_out));  // open: cin, cout
  Subtractor subtractor_3 (
    .a(demultiplexer_3_out1), .b(bit_extender_1_out), .out(subtractor_3_out), .bout(subtractor_3_bout));  // open: bin
  Adder adder_4 (.a(demultiplexer_4_out0), .b(bit_extender_2_out), .out(adder_4_out));  // open: cin, cout
  Subtractor subtractor_4 (
    .a(demultiplexer_4_out1), .b(bit_extender_2_out), .out(subtractor_4_out), .bout(subtractor_4_bout));  // open: bin
  and and_1 (Right_bat_reflection, Right_bat_Y_collision, comparator_1_gt);
  Comparator #(.mode("unsigned")) comparator_1 (.a(adder_1_out), .b(8'hf7), .gt(comparator_1_gt));  // open: eq, lt
  Demultiplexer #(.width(8), .disabled(0), .enable("false")) demultiplexer_7 (
    .out0(demultiplexer_7_out0), .out1(demultiplexer_7_out1), .in(adder_1_out), .sel(Right_bat_reflection));
  Demultiplexer #(.width(8), .disabled(0), .enable("false")) demultiplexer_8 (
    .out0(demultiplexer_8_out0), .out1(demultiplexer_8_out1), .in(subtractor_1_out), .sel(Left_bat_reflection));
  Comparator #(.mode("unsigned")) comparator_2 (.a(subtractor_1_out), .b(8'h8), .lt(comparator_2_lt));  // open: gt, eq
  and and_2 (Left_bat_reflection, comparator_2_lt, Left_bat_Y_collision);
  assign not_1_out = ~demultiplexer_5_out1;  // NOT_Gate not_1, 8 bits wide
  Subtractor subtractor_5 (.a(not_1_out), .b(8'h1), .out(subtractor_5_out));  // open: bin, bout
  Negator negator_1 (.in(demultiplexer_6_out1), .out(negator_1_out));
  and and_3 (and_3_out[0], Left_changed, Left_bat_reflection);
  or or_1 (xor_3_out[1], and_3_out[0], and_3_out[1]);
  and and_4 (and_3_out[1], Right_bat_reflection, Right_changed);
  Multiplexer #(.select(2), .width(4), .enable("false")) multiplexer_1 (
    .in0(4'b0000), .in1(Speed_Left_bat), .in2(Speed_Right_bat), .out(multiplexer_1_out), .sel(and_3_out));  // open: in3
  Multiplexer #(.width(8), .enable("false")) multiplexer_2 (
    .in0(adder_3_out), .in1(8'he7), .out(multiplexer_2_out), .sel(comparator_3_gt));
  Comparator #(.mode("unsigned")) comparator_3 (.a(adder_3_out), .b(8'he7), .gt(comparator_3_gt));  // open: eq, lt
  Multiplexer #(.width(8), .enable("false")) multiplexer_3 (
    .in0(subtractor_3_out), .in1({8{1'b0}}), .out(multiplexer_3_out), .sel(subtractor_3_bout));
  Multiplexer #(.width(8), .enable("false")) multiplexer_4 (
    .in0(adder_4_out), .in1(8'he7), .out(multiplexer_4_out), .sel(comparator_4_gt));
  Comparator #(.mode("unsigned")) comparator_4 (.a(adder_4_out), .b(8'he7), .gt(comparator_4_gt));  // open: eq, lt
  Multiplexer #(.width(8), .enable("false")) multiplexer_5 (
    .in0(subtractor_4_out), .in1({8{1'b0}}), .out(multiplexer_5_out), .sel(subtractor_4_bout));
  assign not_2_out = ~demultiplexer_7_out1;  // NOT_Gate not_2, 8 bits wide
  assign not_3_out = ~demultiplexer_8_out1;  // NOT_Gate not_3, 8 bits wide
  Multiplexer #(.width(8), .enable("false")) multiplexer_6 (
    .in0(demultiplexer_5_out0), .in1(subtractor_5_out), .out(multiplexer_6_out), .sel(adder_2_cout));
  Multiplexer #(.width(8), .enable("false")) multiplexer_7 (
    .in0(demultiplexer_6_out0), .in1(negator_1_out), .out(multiplexer_7_out), .sel(subtractor_2_bout));
  xor xor_1 (New_Y_direction, Change_Y_direction, V[3]);
  xor xor_2 (New_V[4], V[4], Change_X_direction);
  Multiplexer #(.width(8), .enable("false")) multiplexer_8 (
    .in0(multiplexer_2_out), .in1(multiplexer_3_out), .out(New_Left_bat), .sel(Speed_Left_bat[3]));
  Multiplexer #(.width(8), .enable("false")) multiplexer_9 (
    .in0(multiplexer_4_out), .in1(multiplexer_5_out), .out(New_Right_bat), .sel(Speed_Right_bat[3]));
  Adder adder_5 (.a(not_2_out), .b(8'hef), .out(adder_5_out));  // open: cin, cout
  Subtractor subtractor_6 (.a(not_3_out), .b(8'hef), .out(subtractor_6_out));  // open: bin, bout
  Multiplexer #(.width(8), .enable("false")) multiplexer_10 (
    .in0(multiplexer_6_out), .in1(multiplexer_7_out), .out(New_Y_ball), .sel(V[3]));
  xor xor_3 (xor_3_out[0], multiplexer_1_out[3], New_Y_direction);
  Demultiplexer #(.select(2), .width(4), .enable("false")) demultiplexer_9 (
    .out0(demultiplexer_9_out0), .out1(demultiplexer_9_out1),
    .out2({demultiplexer_9_out2_2[3], demultiplexer_9_out2}), .out3(demultiplexer_9_out3),
    .in({New_Y_direction, V[2:0]}), .sel(xor_3_out));
  Comparator #(.mode("unsigned")) comparator_5 (.a(Left_bat), .b(New_Left_bat), .eq(comparator_5_eq));  // open: gt, lt
  Comparator #(.mode("unsigned")) comparator_6 (
    .a(Right_bat), .b(New_Right_bat), .eq(comparator_6_eq));  // open: gt, lt
  Multiplexer #(.width(8), .enable("false")) multiplexer_11 (
    .in0(demultiplexer_7_out0), .in1(adder_5_out), .out(multiplexer_11_out), .sel(Right_bat_reflection));
  Multiplexer #(.width(8), .enable("false")) multiplexer_12 (
    .in0(multiplexer_11_out), .in1(multiplexer_13_out), .out(New_X_ball), .sel(V[4]));
  Multiplexer #(.width(8), .enable("false")) multiplexer_13 (
    .in0(demultiplexer_8_out0), .in1(subtractor_6_out), .out(multiplexer_13_out), .sel(Left_bat_reflection));
  or or_2 (Change_Y_direction, adder_2_cout, and_5_out);
  and and_5 (and_5_out, subtractor_2_bout, V[3]);
  assign bit_extender_4_out = {{5{1'b0}}, multiplexer_1_out[2:0]};  // Bit_Extender bit_extender_4
  Multiplexer #(.width(8), .enable("false")) multiplexer_14 (
    .in0(8'h1), .in1(8'h2), .out(multiplexer_14_out), .sel(in_3));
  not not_4 (Left_changed, comparator_5_eq);
  not not_5 (Right_changed, comparator_6_eq);
  assign bit_extender_5_out = {{5{1'b0}}, demultiplexer_9_out2};  // Bit_Extender bit_extender_5
  assign bit_extender_6_out = {{5{1'b0}}, demultiplexer_9_out3[2:0]};  // Bit_Extender bit_extender_6
  Multiplexer #(.width(8), .enable("false")) multiplexer_15 (
    .in0(8'h3), .in1(8'h1), .out(multiplexer_15_out), .sel(in_3));
  or or_3 (Change_X_direction, Right_bat_reflection, Left_bat_reflection);
  _8_to_5 u_8_to_5_1 (.in_1(New_Y_ball), .out_2(New_Y_ball5));
  Multiplier multiplier_1 (.a(bit_extender_5_out), .b(multiplexer_14_out), .out(multiplier_1_out));  // open: cin, cout
  Multiplier multiplier_2 (.a(bit_extender_6_out), .b(multiplexer_14_out), .out(multiplier_2_out));  // open: cin, cout
  Multiplier multiplier_3 (.a(bit_extender_4_out), .b(multiplexer_15_out), .out(multiplier_3_out));  // open: cin, cout
  Adder adder_6 (.a(multiplexer_14_out), .b(multiplexer_15_out), .out(adder_6_out));  // open: cin, cout
  _8_to_5 u_8_to_5_2 (.in_1(New_Left_bat), .out_2(n8_to_5_2_out_2));
  _8_to_5 u_8_to_5_3 (.in_1(New_Right_bat), .out_2(n8_to_5_3_out_2));
  Adder adder_7 (.a(multiplier_1_out), .b(multiplier_3_out), .out(adder_7_out));  // open: cin, cout
  devision_with_rounding devision_with_rounding_1 (
    .in_1(adder_7_out), .in_2(adder_6_out), .out_3(devision_with_rounding_1_out_3));
  Subtractor subtractor_7 (
    .a(multiplier_2_out), .b(multiplier_3_out), .out(subtractor_7_out), .bout(subtractor_7_bout));  // open: bin
  Negator negator_2 (.in(subtractor_7_out), .out(negator_2_out));
  BitSelector #(.width(32)) bitselector_1 (.in(shifter_1_out), .out(Left_bat_Y_collision), .sel(New_Y_ball5));
  Shifter #(.width(32)) shifter_1 (.in(32'hf), .\dist (n8_to_5_2_out_2), .out(shifter_1_out));
  Shifter #(.width(32)) shifter_2 (.in(32'hf), .\dist (n8_to_5_3_out_2), .out(shifter_2_out));
  BitSelector #(.width(32)) bitselector_2 (.in(shifter_2_out), .out(Right_bat_Y_collision), .sel(New_Y_ball5));
  Bit_Extender #(.out_width(3)) bit_extender_7 (.in(devision_with_rounding_1_out_3), .out(bit_extender_7_out));
  Multiplexer #(.width(8), .enable("false")) multiplexer_16 (
    .in0(subtractor_7_out), .in1(negator_2_out), .out(multiplexer_16_out), .sel(subtractor_7_bout));
  devision_with_rounding devision_with_rounding_2 (
    .in_1(multiplexer_16_out), .in_2(adder_6_out), .out_3(devision_with_rounding_2_out_3));
  Bit_Extender #(.out_width(3)) bit_extender_8 (.in(devision_with_rounding_2_out_3), .out(bit_extender_8_out));
  xor xor_4 (xor_4_out[3], subtractor_7_bout, demultiplexer_9_out3[3]);
  Multiplexer #(.select(2), .width(4), .enable("false")) multiplexer_17 (
    .in0(demultiplexer_9_out0), .in1(demultiplexer_9_out1),
    .in2({demultiplexer_9_out2_2[3], bit_extender_7_out}), .in3({xor_4_out[3], bit_extender_8_out}),
    .out(New_V[3:0]), .sel(xor_3_out));

  // Other names for the same wires on the sheet: Y_speed_direction = V[3]; X_speed_direction = V[4]
endmodule

module CDM8 (
  input  in_1,
  input  [7:0] BallX,
  input  [7:0] BallY,
  input  [4:0] speed,
  output [7:0] calc_bat_pos
);

  wire and_3_out, and_4_out, and_5_out, cdm_8_mark5_1_p4, cdm_8_mark5_1_p6, cdm_8_mark5_1_p7,
       cdm_8_mark5_1_p8, cdm_8_mark5_1_p9, cdm_8_mark5_1_p10, cdm_8_mark5_1_p11, code, data, decoder_2_out0,
       decoder_2_out1, decoder_2_out2, decoder_2_out3, IAck, IOsel, IRQ, load, mem, nand_1_out, not_1_out,
       not_2_out, not_3_out, RAM, READwrite;
  wire [2:0] vec;
  wire [3:0] IOaddr;
  wire [7:0] cdm_8_mark5_1_p15, cdm_8_mark5_1_p16, IOdat, register_1_q, register_2_q, register_3_q;
  wire [7:4] cdm_8_mark5_1_p14;

  and and_1 (IOsel, not_1_out, in_1, data);
  // Probe on cdm_8_mark5_1_p6
  // Probe on cdm_8_mark5_1_p4
  // Probe on cdm_8_mark5_1_p7
  // Probe on nothing
  not not_1 (not_1_out, nand_1_out);
  // Probe on cdm_8_mark5_1_p8
  // Probe on cdm_8_mark5_1_p9
  // Probe on cdm_8_mark5_1_p10
  // CdM_8_mark5 cdm_8_mark5_1: pin names not known; wires that end beside it: IRQ, vec, IAck, cdm_8_mark5_1_p4, in_1, cdm_8_mark5_1_p6, cdm_8_mark5_1_p7, cdm_8_mark5_1_p8, cdm_8_mark5_1_p9, cdm_8_mark5_1_p10, cdm_8_mark5_1_p11, mem, READwrite, {cdm_8_mark5_1_p14, IOaddr}, cdm_8_mark5_1_p15, cdm_8_mark5_1_p16
  nand nand_1 (nand_1_out, cdm_8_mark5_1_p14[4], cdm_8_mark5_1_p14[5], cdm_8_mark5_1_p14[6], cdm_8_mark5_1_p14[7]);
  and and_2 (RAM, nand_1_out, data);
  Decoder #(.disabled(0)) decoder_1 (.out0(code), .out1(data), .sel(cdm_8_mark5_1_p11), .en(mem));
  not not_2 (not_2_out, READwrite);
  assign IOdat = not_2_out ? cdm_8_mark5_1_p15 : 8'bz;  // Controlled_Buffer controlled_buffer_1
  assign cdm_8_mark5_1_p16 = READwrite ? IOdat : 8'bz;  // Controlled_Buffer controlled_buffer_2
  Register register_1 (.D(BallX), .Q(register_1_q), .clk(load));  // open: en, clr
  Register register_2 (.D(BallY), .Q(register_2_q), .clk(load));  // open: en, clr
  Register register_3 (.D({speed[4], 3'b100, speed[3:0]}), .Q(register_3_q), .clk(load));  // open: en, clr
  assign IOdat = and_3_out ? register_1_q : 8'bz;  // Controlled_Buffer controlled_buffer_3
  and and_3 (and_3_out, IOsel, READwrite, decoder_2_out0);
  assign IOdat = and_4_out ? register_2_q : 8'bz;  // Controlled_Buffer controlled_buffer_4
  and and_4 (and_4_out, IOsel, READwrite, decoder_2_out1);
  assign IOdat = and_5_out ? register_3_q : 8'bz;  // Controlled_Buffer controlled_buffer_5
  and and_5 (and_5_out, IOsel, READwrite, decoder_2_out2);
  Register register_4 (.D(IOdat), .Q(calc_bat_pos), .clk(load));  // open: en, clr
  and and_6 (load, decoder_2_out3, ~READwrite, IOsel);  // AND_Gate
  RAM ram_1 (
    .addr({cdm_8_mark5_1_p14, IOaddr}), .data(IOdat), .sel(RAM), .clk(not_3_out), .ld(READwrite));  // open: clr
  not not_3 (not_3_out, in_1);
  ROM rom_1 (.addr({cdm_8_mark5_1_p14, IOaddr}), .data(IOdat), .sel(code));
  Decoder #(.select(4), .enable("false")) decoder_2 (
    .out0(decoder_2_out0), .out1(decoder_2_out1), .out2(decoder_2_out2), .out3(decoder_2_out3), .sel(IOaddr));  // open: out4, out5, out6, out7, out8, out9, out10, out11, out12, out13, out14, out15

  // Other names for the same wires on the sheet: clk = in_1

  // Notes on the sheet:
  //   contents of rom_1 (hex, n*v repeats v):
  //   d1 f2 b5 d2 80 46 e4 36 d0 f0 b0 d2 fb 38 3f f 90 f 90 d2 8 46 d3 7 4d d3 f1 bf a e0 24 d2 1 83 ee
  //   25 3a 5 e0 30 13 e3 2d 8e 8f 89 ee 25 92 e3 34 83 ee 38 d3 80 d0 f3 a3 ee 0 d4 180*0 4f
endmodule

module video_section (
  input  in_1,
  input  [4:0] ID_input,
  input  [4:0] X_ball,
  input  [31:0] Y_ball,
  input  [31:0] Left_bat,
  input  [31:0] Right_bat,
  input  [31:0] in_7,
  input  [31:0] in_8,
  input  [31:0] in_9,
  input  [31:0] in_10,
  input  [31:0] in_11,
  input  [31:0] in_12,
  input  [31:0] in_13,
  input  [31:0] in_14,
  output [31:0] out_15,
  output [31:0] out_16,
  output [31:0] out_17,
  output [31:0] out_18,
  output [31:0] out_19,
  output [31:0] out_20,
  output [31:0] out_21,
  output [31:0] out_22,
  output out_23,
  output [4:0] ID_output,
  output [4:0] X_output,
  output [31:0] Y_output,
  output [31:0] Left_bat_2,
  output [31:0] Right_bat_2
);

  wire comparator_1_eq, comparator_2_eq, comparator_3_eq, comparator_4_eq, comparator_5_eq, comparator_6_eq,
       comparator_7_eq, comparator_8_eq, comparator_9_eq, comparator_10_eq;
  wire [4:0] inc_5bit_1_output, inc_5bit_2_output, inc_5bit_3_output, inc_5bit_4_output, inc_5bit_5_output,
       inc_5bit_6_output, inc_5bit_7_output;
  wire [31:0] multiplexer_2_out, multiplexer_17_out, or_1_out, or_2_out, out1, out2, out3, out4, out5, out6,
       out7, out8;

  Multiplexer #(.width(32), .enable("false")) multiplexer_1 (
    .in0(multiplexer_2_out), .in1(or_1_out), .out(out1), .sel(comparator_1_eq));
  Comparator #(.width(5)) comparator_1 (.a({5{1'b0}}), .b(ID_input), .eq(comparator_1_eq));  // open: gt, lt
  Multiplexer #(.width(32), .enable("false")) multiplexer_2 (
    .in0({32{1'b0}}), .in1(Y_ball), .out(multiplexer_2_out), .sel(comparator_2_eq));
  inc_5bit inc_5bit_1 (.\input (ID_input), .\output (inc_5bit_1_output));
  Comparator #(.width(5)) comparator_2 (.a(ID_input), .b(X_ball), .eq(comparator_2_eq));  // open: gt, lt
  assign or_1_out = multiplexer_2_out | Left_bat;  // OR_Gate or_1, 32 bits wide
  Comparator #(.width(5)) comparator_3 (.a(inc_5bit_1_output), .b(X_ball), .eq(comparator_3_eq));  // open: gt, lt
  Multiplexer #(.width(32), .enable("false")) multiplexer_3 (.in0(out1), .in1(in_7), .out(out_15), .sel(in_1));
  Multiplexer #(.width(32), .enable("false")) multiplexer_4 (
    .in0({32{1'b0}}), .in1(Y_ball), .out(out2), .sel(comparator_3_eq));
  inc_5bit inc_5bit_2 (.\input (inc_5bit_1_output), .\output (inc_5bit_2_output));
  Multiplexer #(.width(32), .enable("false")) multiplexer_5 (.in0(out2), .in1(in_8), .out(out_16), .sel(in_1));
  Comparator #(.width(5)) comparator_4 (.a(inc_5bit_2_output), .b(X_ball), .eq(comparator_4_eq));  // open: gt, lt
  Multiplexer #(.width(32), .enable("false")) multiplexer_6 (
    .in0({32{1'b0}}), .in1(Y_ball), .out(out3), .sel(comparator_4_eq));
  inc_5bit inc_5bit_3 (.\input (inc_5bit_2_output), .\output (inc_5bit_3_output));
  Multiplexer #(.width(32), .enable("false")) multiplexer_7 (.in0(out3), .in1(in_9), .out(out_17), .sel(in_1));
  Comparator #(.width(5)) comparator_5 (.a(inc_5bit_3_output), .b(X_ball), .eq(comparator_5_eq));  // open: gt, lt
  Multiplexer #(.width(32), .enable("false")) multiplexer_8 (.in0(out4), .in1(in_10), .out(out_18), .sel(in_1));
  Multiplexer #(.width(32), .enable("false")) multiplexer_9 (
    .in0({32{1'b0}}), .in1(Y_ball), .out(out4), .sel(comparator_5_eq));
  inc_5bit inc_5bit_4 (.\input (inc_5bit_3_output), .\output (inc_5bit_4_output));
  Multiplexer #(.width(32), .enable("false")) multiplexer_10 (.in0(out5), .in1(in_11), .out(out_19), .sel(in_1));
  Comparator #(.width(5)) comparator_6 (.a(inc_5bit_4_output), .b(X_ball), .eq(comparator_6_eq));  // open: gt, lt
  Multiplexer #(.width(32), .enable("false")) multiplexer_11 (.in0(out6), .in1(in_12), .out(out_20), .sel(in_1));
  Multiplexer #(.width(32), .enable("false")) multiplexer_12 (
    .in0({32{1'b0}}), .in1(Y_ball), .out(out5), .sel(comparator_6_eq));
  inc_5bit inc_5bit_5 (.\input (inc_5bit_4_output), .\output (inc_5bit_5_output));
  Comparator #(.width(5)) comparator_7 (.a(inc_5bit_5_output), .b(X_ball), .eq(comparator_7_eq));  // open: gt, lt
  Multiplexer #(.width(32), .enable("false")) multiplexer_13 (.in0(out7), .in1(in_13), .out(out_21), .sel(in_1));
  Multiplexer #(.width(32), .enable("false")) multiplexer_14 (
    .in0({32{1'b0}}), .in1(Y_ball), .out(out6), .sel(comparator_7_eq));
  inc_5bit inc_5bit_6 (.\input (inc_5bit_5_output), .\output (inc_5bit_6_output));
  Multiplexer #(.width(32), .enable("false")) multiplexer_15 (.in0(out8), .in1(in_14), .out(out_22), .sel(in_1));
  Multiplexer #(.width(32), .enable("false")) multiplexer_16 (
    .in0({32{1'b0}}), .in1(Y_ball), .out(out7), .sel(comparator_8_eq));
  inc_5bit inc_5bit_7 (.\input (inc_5bit_6_output), .\output (inc_5bit_7_output));
  Comparator #(.width(5)) comparator_8 (.a(inc_5bit_6_output), .b(X_ball), .eq(comparator_8_eq));  // open: gt, lt
  Comparator #(.width(5)) comparator_9 (.a({5{1'b1}}), .b(inc_5bit_7_output), .eq(comparator_9_eq));  // open: gt, lt
  Multiplexer #(.width(32), .enable("false")) multiplexer_17 (
    .in0({32{1'b0}}), .in1(Y_ball), .out(multiplexer_17_out), .sel(comparator_10_eq));
  inc_5bit inc_5bit_8 (.\input (inc_5bit_7_output), .\output (ID_output));
  Comparator #(.width(5)) comparator_10 (.a(inc_5bit_7_output), .b(X_ball), .eq(comparator_10_eq));  // open: gt, lt
  Multiplexer #(.width(32), .enable("false")) multiplexer_18 (
    .in0(multiplexer_17_out), .in1(or_2_out), .out(out8), .sel(comparator_9_eq));
  assign or_2_out = multiplexer_17_out | Right_bat;  // OR_Gate or_2, 32 bits wide

  assign Left_bat_2 = Left_bat;
  assign out_23 = in_1;
  assign Right_bat_2 = Right_bat;
  assign X_output = X_ball;
  assign Y_output = Y_ball;

  // Other names for the same wires on the sheet: game_1[31:0] = in_7; game_2[31:0] = in_8; game_3[31:0] = in_9;
  //   game_4[31:0] = in_10; game_5[31:0] = in_11; game_6[31:0] = in_12; game_7[31:0] = in_13; game_8[31:0] = in_14
endmodule

module game_end_screen_and_settings (
  input  in_1,
  input  Weight,
  input  \Сomplexity ,
  input  Color,
  output [31:0] out_5,
  output [31:0] out_6,
  output [31:0] out_7,
  output [31:0] out_8,
  output [31:0] out_9,
  output [31:0] out_10,
  output [31:0] out_11,
  output [31:0] out_12,
  output [31:0] out_13,
  output [31:0] out_14,
  output [31:0] out_15,
  output [31:0] out_16,
  output [31:0] out_17,
  output [31:0] out_18,
  output [31:0] out_19,
  output [31:0] out_20,
  output [31:0] out_21,
  output [31:0] out_22,
  output [31:0] out_23,
  output [31:0] out_24,
  output [31:0] out_25,
  output [31:0] out_26,
  output [31:0] out_27,
  output [31:0] out_28,
  output [31:0] out_29,
  output [31:0] out_30,
  output [31:0] out_31,
  output [31:0] out_32,
  output [31:0] out_33,
  output [31:0] out_34,
  output [31:0] out_35,
  output [31:0] out_36,
  output Light,
  output Heavy,
  output _0,
  output _1,
  output _2,
  output [3:0] Settings
);

  Multiplexer #(.width(32), .enable("false")) multiplexer_1 (
    .in0({32{1'b0}}), .in1({32{1'b0}}), .out(out_5), .sel(in_1));
  Multiplexer #(.width(32), .enable("false")) multiplexer_2 (
    .in0({32{1'b0}}), .in1({32{1'b0}}), .out(out_6), .sel(in_1));
  Multiplexer #(.width(32), .enable("false")) multiplexer_3 (
    .in0(32'h7ffe00), .in1(32'h7ffe00), .out(out_7), .sel(in_1));
  Counter #(.width(1), .max('h1)) counter_1 (.Q(Heavy), .clk(Weight));  // open: load, D, count, carry, clr
  Multiplexer #(.width(32), .enable("false")) multiplexer_4 (
    .in0(32'h400200), .in1(32'h400200), .out(out_8), .sel(in_1));
  not not_1 (Light, Heavy);
  Multiplexer #(.width(32), .enable("false")) multiplexer_5 (
    .in0(32'h5f0200), .in1(32'h5f0200), .out(out_9), .sel(in_1));
  Counter #(.width(2), .max('h2)) counter_2 (
    .Q({_2, Settings[1]}), .clk(\Сomplexity ));  // open: load, D, count, carry, clr
  or or_1 (_1, Settings[1], _2);
  Multiplexer #(.width(32), .enable("false")) multiplexer_6 (
    .in0(32'h41fa00), .in1(32'h41fa00), .out(out_10), .sel(in_1));
  Multiplexer #(.width(32), .enable("false")) multiplexer_7 (
    .in0(32'h5f0200), .in1(32'h5f0200), .out(out_11), .sel(in_1));
  Counter #(.width(1), .max('h1)) counter_3 (.Q(Settings[3]), .clk(Color));  // open: load, D, count, carry, clr
  Multiplexer #(.width(32), .enable("false")) multiplexer_8 (
    .in0(32'h40fa00), .in1(32'h40fa00), .out(out_12), .sel(in_1));
  Multiplexer #(.width(32), .enable("false")) multiplexer_9 (
    .in0(32'h408a00), .in1(32'h408a00), .out(out_13), .sel(in_1));
  Multiplexer #(.width(32), .enable("false")) multiplexer_10 (
    .in0(32'h40fa00), .in1(32'h40fa00), .out(out_14), .sel(in_1));
  Multiplexer #(.width(32), .enable("false")) multiplexer_11 (
    .in0(32'h400200), .in1(32'h400200), .out(out_15), .sel(in_1));
  Multiplexer #(.width(32), .enable("false")) multiplexer_12 (
    .in0(32'h40fa00), .in1(32'h40fa00), .out(out_16), .sel(in_1));
  Multiplexer #(.width(32), .enable("false")) multiplexer_13 (
    .in0(32'h400a00), .in1(32'h400a00), .out(out_17), .sel(in_1));
  Multiplexer #(.width(32), .enable("false")) multiplexer_14 (
    .in0(32'h40fa00), .in1(32'h40fa00), .out(out_18), .sel(in_1));
  Multiplexer #(.width(32), .enable("false")) multiplexer_15 (
    .in0(32'h400200), .in1(32'h400200), .out(out_19), .sel(in_1));
  Multiplexer #(.width(32), .enable("false")) multiplexer_16 (
    .in0(32'h400200), .in1(32'h400200), .out(out_20), .sel(in_1));
  Multiplexer #(.width(32), .enable("false")) multiplexer_17 (
    .in0(32'h5ffa00), .in1(32'h5ff200), .out(out_21), .sel(in_1));
  Multiplexer #(.width(32), .enable("false")) multiplexer_18 (
    .in0(32'h400200), .in1(32'h400a00), .out(out_22), .sel(in_1));
  Multiplexer #(.width(32), .enable("false")) multiplexer_19 (
    .in0(32'h40fa00), .in1(32'h43fa00), .out(out_23), .sel(in_1));
  Multiplexer #(.width(32), .enable("false")) multiplexer_20 (
    .in0(32'h408a00), .in1(32'h400a00), .out(out_24), .sel(in_1));
  Multiplexer #(.width(32), .enable("false")) multiplexer_21 (
    .in0(32'h40fa00), .in1(32'h5ff200), .out(out_25), .sel(in_1));
  Multiplexer #(.width(32), .enable("false")) multiplexer_22 (
    .in0(32'h400200), .in1(32'h400200), .out(out_26), .sel(in_1));
  Multiplexer #(.width(32), .enable("false")) multiplexer_23 (
    .in0(32'h40ea00), .in1(32'h40ba00), .out(out_27), .sel(in_1));
  Multiplexer #(.width(32), .enable("false")) multiplexer_24 (
    .in0(32'h40ba00), .in1(32'h400200), .out(out_28), .sel(in_1));
  Multiplexer #(.width(32), .enable("false")) multiplexer_25 (
    .in0(32'h400200), .in1(32'h40fa00), .out(out_29), .sel(in_1));
  Multiplexer #(.width(32), .enable("false")) multiplexer_26 (
    .in0(32'h40fa00), .in1(32'h408200), .out(out_30), .sel(in_1));
  Multiplexer #(.width(32), .enable("false")) multiplexer_27 (
    .in0(32'h40aa00), .in1(32'h407a00), .out(out_31), .sel(in_1));
  Multiplexer #(.width(32), .enable("false")) multiplexer_28 (
    .in0(32'h400200), .in1(32'h400200), .out(out_32), .sel(in_1));
  Multiplexer #(.width(32), .enable("false")) multiplexer_29 (
    .in0(32'h400200), .in1(32'h400200), .out(out_33), .sel(in_1));
  Multiplexer #(.width(32), .enable("false")) multiplexer_30 (
    .in0(32'h7ffe00), .in1(32'h7ffe00), .out(out_34), .sel(in_1));
  Multiplexer #(.width(32), .enable("false")) multiplexer_31 (
    .in0({32{1'b0}}), .in1({32{1'b0}}), .out(out_35), .sel(in_1));
  Multiplexer #(.width(32), .enable("false")) multiplexer_32 (
    .in0({32{1'b0}}), .in1({32{1'b0}}), .out(out_36), .sel(in_1));

  assign _0 = 1'b1;
  assign {Settings[2], Settings[0]} = {_2, Heavy};

  // Other names for the same wires on the sheet: game = in_1

  // Notes on the sheet:
  //   Lose
  //   Win
  //   Settings
endmodule

module inc_score (
  input  [7:0] \input ,
  output [7:0] \output 
);

  wire comparator_1_gt, comparator_2_gt;
  wire [3:0] adder_1_out, adder_2_out;

  Adder #(.width(4)) adder_1 (.a(4'b0001), .b(\input [3:0]), .out(adder_1_out));  // open: cin, cout
  Comparator #(.width(4), .mode("unsigned")) comparator_1 (
    .a(adder_1_out), .b(4'b1001), .gt(comparator_1_gt));  // open: eq, lt
  Multiplexer #(.width(4), .disabled(0), .enable("false")) multiplexer_1 (
    .in0(adder_1_out), .in1(4'b0000), .out(\output [3:0]), .sel(comparator_1_gt));
  Adder #(.width(4)) adder_2 (.a(\input [7:4]), .b(4'b0000), .out(adder_2_out), .cin(comparator_1_gt));  // open: cout
  Comparator #(.width(4), .mode("unsigned")) comparator_2 (
    .a(adder_2_out), .b(4'b1001), .gt(comparator_2_gt));  // open: eq, lt
  Multiplexer #(.width(4), .disabled(0), .enable("false")) multiplexer_2 (
    .in0(adder_2_out), .in1(4'b0000), .out(\output [7:4]), .sel(comparator_2_gt));
endmodule

module inc_5bit (
  input  [4:0] \input ,
  output [4:0] \output 
);

  Adder #(.width(5)) adder_1 (.a(\input ), .b(5'b00001), .out(\output ));  // open: cin, cout
endmodule

module game_over (
  input  [7:0] player,
  input  [7:0] cdm8,
  output win,
  output game_over,
  output lose
);

  Comparator comparator_1 (.a(player), .b(8'h11), .eq(win));  // open: gt, lt
  Comparator comparator_2 (.a(cdm8), .b(8'h11), .eq(lose));  // open: gt, lt
  or or_1 (game_over, win, lose);
endmodule

module devision_with_rounding (
  input  [7:0] in_1,
  input  [7:0] in_2,
  output [7:0] out_3
);

  wire comparator_1_lt, not_1_out;
  wire [7:0] adder_1_out, divider_1_out, divider_1_rem, shifter_1_out;

  Divider divider_1 (.a(in_1), .b(in_2), .out(divider_1_out), .rem(divider_1_rem));  // open: upper
  Adder adder_1 (.a(divider_1_out), .b(8'h1), .out(adder_1_out));  // open: cin, cout
  Shifter shifter_1 (.in(divider_1_rem), .\dist (3'b001), .out(shifter_1_out));
  Multiplexer #(.width(8), .enable("false")) multiplexer_1 (
    .in0(divider_1_out), .in1(adder_1_out), .out(out_3), .sel(not_1_out));
  not not_1 (not_1_out, comparator_1_lt);
  Comparator #(.mode("unsigned")) comparator_1 (.a(shifter_1_out), .b(in_2), .lt(comparator_1_lt));  // open: gt, eq
endmodule

module _8_to_5 (
  input  [7:0] in_1,
  output [4:0] out_2
);


  assign out_2 = in_1[7:3];
endmodule
